# Fritzing sketch compressor (saved by Fritzing 1.0.5)
circuit board: 20cm x 20cm
breadboards: 2

parts:
  DC-DC_WAVGAT_mini560_9V = mini560 [package=THT]
  Спикер = Passive Buzzer
  Реле = 2-Channel 5v Relay Shield [package=relay-2ch5v10a]
  Драйвер_мотора = H-Bridge with L298N
  Arduino_UNO_R3 = Arduino Uno (Rev3)
  DC-DC_WAVGAT_mini560_5V = mini560 [package=THT]
  R1 = Resistor [tolerance=±5% power=0.25W resistance=1k package=THT]
  Мосфет = IFR520 MOS module [package=THT]
  Relay1 = Mini Power Relay-HK19F [package=HK19F]

nets:
  GND: DC-DC_WAVGAT_mini560_9V.pin_3, DC-DC_WAVGAT_mini560_9V.pin_4, DC-DC_WAVGAT_mini560_9V.pin_6, DC-DC_WAVGAT_mini560_9V.pin_7, Спикер.-, Реле.GND, Драйвер_мотора.GND, Arduino_UNO_R3.GND, DC-DC_WAVGAT_mini560_5V.pin_3, DC-DC_WAVGAT_mini560_5V.pin_6, DC-DC_WAVGAT_mini560_5V.pin_7, Мосфет.pin3, Мосфет.pin7, Relay1.COIL#15
  N1: DC-DC_WAVGAT_mini560_9V.pin_8, DC-DC_WAVGAT_mini560_9V.pin_9, Arduino_UNO_R3.VIN
  N2: Спикер.S, Arduino_UNO_R3.D10_PWM/SS
  VCC: Спикер.NC, Реле.VCC, Arduino_UNO_R3.5V, R1.Pin_0, Мосфет.pin2
  N3: Реле.IN1, Arduino_UNO_R3.D7
  N4: Реле.IN2, Arduino_UNO_R3.D4
  N5: Реле.JD-VCC, Arduino_UNO_R3.D2, DC-DC_WAVGAT_mini560_5V.pin_8, DC-DC_WAVGAT_mini560_5V.pin_9, Relay1.COIL#0
  N6: Драйвер_мотора.ENA, Arduino_UNO_R3.D3_PWM
  N7: Драйвер_мотора.IN1, Arduino_UNO_R3.D5_PWM
  N8: Драйвер_мотора.IN2, Arduino_UNO_R3.D6_PWM
  N9: Arduino_UNO_R3.A0, Relay1.NO_A
  N10: Arduino_UNO_R3.A4/SDA, R1.Pin_1
  N11: Arduino_UNO_R3.D9_PWM, Мосфет.pin1

notes:
  +12V с задержкой выключения
  GND
  +12V с кнопки включения
  ДТВ 1 OUT
  ДПДЗ main OUT
  ДПДЗ 1 OUT
  ДПДЗ 2 OUT

custom parts:
  mini560: 5A DC-DC Mini 560 Step Down Stabilized Voltage Supply Module Output 3.3 5V 9V 12V Step-down Power Converter Board Module
  2-Channel 5v Relay Shield: 2 Channel 5v Relay Shield w. 2x SPD-06VDC-SD-C
  H-Bridge with L298N: h-bridge
  Mini Power Relay-HK19F: DC 3V, 5V, 6V, 9V, 12V, and, 24V Coil DPDT 8 Pin 2NO 2NC Mini Power Relays PCB Type HK19F
